// Logisim project control_logic.circ as structural Verilog: 1 circuit, main circuit control_logic
module control_logic (
  input  [31:0] inst,
  input  BrEq,
  input  BrLt,
  output PCSel,
  output RegWEn,
  output [2:0] ImmSel,
  output BrUn,
  output ASel,
  output BSel,
  output [3:0] ALUSel,
  output MemRW,
  output [1:0] WBSel,
  output CSRSel,
  output CSRWen
);

  wire alu_and_out, alu_mul_out, alu_mulh_out, alu_mulhu_out, alu_or_out, alu_sll_out, alu_slt_out,
       alu_sra_out, alu_srl_out, alu_sub_out, alu_xor_out, auipct, fq0, fq1, fq20, fs0, fs1, fs2, fs3, fs4,
       fs5, fs6, fs7, it, jalrt, luit, lwt, or_1_out, or_2_out, or_3_out, or_4_out, or_5_out, or_6_out,
       or_7_out, rt, sbt, st;

  or or_1 (or_1_out, rt, it);
  or or_2 (or_2_out, rt, it);
  or or_3 (or_3_out, rt, it);
  or or_4 (or_4_out, rt, it);
  or or_5 (or_5_out, rt, it);
  or or_6 (or_6_out, rt, it);
  or or_7 (or_7_out, rt, it);
  and r_type (rt, inst[0], inst[1], inst[4], inst[5]);
  and lw_type (lwt, inst[0], inst[1]);
  and i_type (it, inst[0], inst[1], inst[4]);
  and i_type_jalr (jalrt, inst[0], inst[1], inst[2], inst[5], inst[6]);
  and s_type (st, inst[0], inst[1], inst[5]);
  and sb_type (sbt, inst[0], inst[1], inst[5], inst[6]);
  and u_type_auipc (auipct, inst[0], inst[1], inst[2], inst[4]);
  and u_type_lui (luit, inst[0], inst[1], inst[2], inst[4], inst[5]);
  and uj_type (ImmSel[2], inst[0], inst[1], inst[2], inst[3], inst[5], inst[6]);
  and alu_and (alu_and_out, fs7, or_1_out);
  and alu_or (alu_or_out, fs6, or_2_out);
  and alu_xor (alu_xor_out, fs4, or_3_out);
  and alu_srl (alu_srl_out, fs5, fq0, or_4_out);
  and alu_sra (alu_sra_out, fs5, fq20, or_5_out);
  and alu_sll (alu_sll_out, fs1, fq0, or_6_out);
  and alu_slt (alu_slt_out, fs2, or_7_out);
  and alu_mul (alu_mul_out, fs0, fq1, rt);
  and alu_mulhu (alu_mulhu_out, fs3, fq1, rt);
  and alu_sub (alu_sub_out, fs0, fq20, rt);
  and alu_mulh (alu_mulh_out, fs1, fq1, rt);
  or or_8 (RegWEn, luit, jalrt, it, lwt, auipct, rt, ImmSel[2]);
  and and_1 (fq0, ~inst[25], ~inst[26], ~inst[27], ~inst[28], ~inst[29], ~inst[30], ~inst[31]);  // AND_Gate
  or or_9 (ImmSel[1], sbt, auipct, luit);
  and and_2 (fq1, inst[25], ~inst[26], ~inst[27], ~inst[28], ~inst[29], ~inst[30], ~inst[31]);  // AND_Gate
  or or_10 (ImmSel[0], st, auipct, luit);
  and and_3 (fq20, ~inst[25], ~inst[26], ~inst[27], ~inst[28], ~inst[29], inst[30], ~inst[31]);  // AND_Gate
  or or_11 (ALUSel[0], alu_and_out, alu_xor_out, alu_sra_out, alu_slt_out, alu_mulhu_out, st);
  or or_12 (ALUSel[1], alu_or_out, alu_xor_out, alu_sll_out, alu_mulh_out, alu_slt_out, alu_mul_out, alu_mulhu_out);
  or or_13 (ALUSel[2], alu_srl_out, alu_sra_out, alu_sll_out, alu_slt_out, alu_sub_out, st, alu_mulh_out);
  or or_14 (ALUSel[3], alu_mul_out, alu_mulhu_out, alu_sub_out, st, alu_mulh_out);
  and and_4 (fs0, ~inst[12], ~inst[13], ~inst[14]);  // AND_Gate
  or or_15 (BSel, lwt, it, jalrt, st, auipct, luit, ImmSel[2]);
  and and_5 (fs1, inst[12], ~inst[13], ~inst[14]);  // AND_Gate
  and and_6 (fs2, ~inst[12], inst[13], ~inst[14]);  // AND_Gate
  and and_7 (fs3, inst[12], inst[13], ~inst[14]);  // AND_Gate
  and and_8 (fs4, ~inst[12], ~inst[13], inst[14]);  // AND_Gate
  and and_9 (fs5, inst[12], ~inst[13], inst[14]);  // AND_Gate
  and and_10 (fs6, ~inst[12], inst[13], inst[14]);  // AND_Gate
  and and_11 (fs7, inst[12], inst[13], inst[14]);

  // Other names for the same wires on the sheet: bimm[11:0] = {inst[31], inst[8], inst[30:25], inst[12:9]};
  //   bimm4_1[3:0] = inst[12:9]; rd[4:0] = inst[11:7]; simm[11:0] = {inst[31:25], inst[12:8]};
  //   funct3[2:0] = inst[14:12]; jimm[19:0] = {inst[31], inst[19:12], inst[20], inst[30:21]};
  //   uimm[19:0] = inst[31:12]; bimm10_5[5:0] = inst[30:25]; funct7[6:0] = inst[31:25]; iimm[11:0] = inst[31:20];
  //   bimm11 = inst[8]; bimm12 = inst[31]; jalt = ImmSel[2]; opcode[6:0] = inst[6:0]; rs2[4:0] = inst[24:20];
  //   rs1[4:0] = inst[19:15]

  // Notes on the sheet:
  //   INPUTS to your circuit
  //   DON'T CHANGE THE LOCATIONS OF THE INPUTS AND OUTPUTS!
  //   OUTPUT from your circuit
  //   000 for i-type
  //   001 for s-type
  //   010 for b-type
  //   011 for u-type
  //   100 for j-type
endmodule
