// Logisim project imm_gen.circ as structural Verilog: 1 circuit, main circuit imm_gen
module imm_gen (
  input  [31:0] inst,
  input  [2:0] ImmSel,
  output [31:0] imm
);

  wire [11:0] multiplexer_5_out;
  wire [12:0] multiplexer_4_out;
  wire [19:0] multiplexer_3_out;
  wire [20:0] multiplexer_1_out, multiplexer_2_out;

  Multiplexer #(.enable("false"), .width(21)) multiplexer_1 (
    .in0({21{1'b0}}), .in1({21{1'b1}}), .out(multiplexer_1_out), .sel(inst[31]));
  Multiplexer #(.enable("false"), .width(21)) multiplexer_2 (
    .in0({21{1'b0}}), .in1({21{1'b1}}), .out(multiplexer_2_out), .sel(inst[31]));
  Multiplexer #(.enable("false"), .width(20)) multiplexer_3 (
    .in0({20{1'b0}}), .in1({20{1'b1}}), .out(multiplexer_3_out), .sel(inst[31]));
  Multiplexer #(.enable("false"), .width(13)) multiplexer_4 (
    .in0({13{1'b0}}), .in1({13{1'b1}}), .out(multiplexer_4_out), .sel(inst[31]));
  Multiplexer #(.enable("false"), .width(12)) multiplexer_5 (
    .in0({12{1'b0}}), .in1({12{1'b1}}), .out(multiplexer_5_out), .sel(inst[31]));
  Multiplexer #(.enable("false"), .select(3), .width(32)) multiplexer_6 (
    .in0({multiplexer_1_out, inst[30:20]}), .in1({multiplexer_2_out, inst[30:25], inst[12:8]}),
    .in2({multiplexer_3_out, inst[8], inst[30:25], inst[12:9], 1'b0}),
    .in3({multiplexer_4_out, inst[30:12]}),
    .in4({multiplexer_5_out, inst[19:12], inst[20], inst[30:21], 1'b0}), .out(imm), .sel(ImmSel));  // open: in5, in6, in7

  // Other names for the same wires on the sheet: bimm[11:0] = {inst[31], inst[8], inst[30:25], inst[12:9]};
  //   bimm4_1[3:0] = inst[12:9]; rd[4:0] = inst[11:7]; simm[11:0] = {inst[31:25], inst[12:8]};
  //   funct3[2:0] = inst[14:12]; jimm[19:0] = {inst[31], inst[19:12], inst[20], inst[30:21]};
  //   uimm[19:0] = inst[31:12]; bimm10_5[5:0] = inst[30:25]; funct7[6:0] = inst[31:25]; iimm[11:0] = inst[31:20];
  //   bimm11 = inst[8]; rs2[4:0] = inst[24:20]; rs1[4:0] = inst[19:15]; bimm12 = inst[31]; opcode[6:0] = inst[6:0]

  // Notes on the sheet:
  //   INPUTS to your circuit
  //   DON'T CHANGE THE LOCATIONS OF THE INPUTS AND OUTPUTS!
  //   OUTPUT from your circuit
endmodule
