// Logisim project regfile.circ as structural Verilog: 1 circuit, main circuit regfile
module regfile (
  input  [4:0] rs1,
  input  [4:0] rs2,
  input  [4:0] rd,
  input  [31:0] Write_Data,
  input  RegWEn,
  input  clk,
  output [31:0] ra,
  output [31:0] sp,
  output [31:0] t0,
  output [31:0] t1,
  output [31:0] t2,
  output [31:0] s0,
  output [31:0] s1,
  output [31:0] a0,
  output [31:0] Read_Data_1,
  output [31:0] Read_Data_2
);

  wire demultiplexer_1_out0, w0, w1, w2, w3, w4, w5, w6, w7, w8, w9, w10, w11, w12, w13, w14, w15, w16, w17,
       w18, w19, w20, w21, w22, w23, w24, w25, w26, w27, w28, w29, w30, w31;
  wire [31:0] x0, x3, x4, x11, x12, x13, x14, x15, x16, x17, x18, x19, x20, x21, x22, x23, x24, x25, x26,
       x27, x28, x29, x30, x31;

  and and_1 (w0, demultiplexer_1_out0, 1'b0);
  Multiplexer #(.enable("false"), .select(5), .width(32)) multiplexer_1 (
    .in0(x0), .in1(ra), .in2(sp), .in3(x3), .in4(x4), .in5(t0), .in6(t1), .in7(t2), .in8(s0), .in9(s1),
    .in10(a0), .in11(x11), .in12(x12), .in13(x13), .in14(x14), .in15(x15), .in16(x16), .in17(x17),
    .in18(x18), .in19(x19), .in20(x20), .in21(x21), .in22(x22), .in23(x23), .in24(x24), .in25(x25),
    .in26(x26), .in27(x27), .in28(x28), .in29(x29), .in30(x30), .in31(x31), .out(Read_Data_1), .sel(rs1));
  Multiplexer #(.enable("false"), .select(5), .width(32)) multiplexer_2 (
    .in0(x0), .in1(ra), .in2(sp), .in3(x3), .in4(x4), .in5(t0), .in6(t1), .in7(t2), .in8(s0), .in9(s1),
    .in10(a0), .in11(x11), .in12(x12), .in13(x13), .in14(x14), .in15(x15), .in16(x16), .in17(x17),
    .in18(x18), .in19(x19), .in20(x20), .in21(x21), .in22(x22), .in23(x23), .in24(x24), .in25(x25),
    .in26(x26), .in27(x27), .in28(x28), .in29(x29), .in30(x30), .in31(x31), .out(Read_Data_2), .sel(rs2));
  Demultiplexer #(.enable("false"), .select(5)) demultiplexer_1 (
    .out0(demultiplexer_1_out0), .out1(w1), .out2(w2), .out3(w3), .out4(w4), .out5(w5), .out6(w6), .out7(w7),
    .out8(w8), .out9(w9), .out10(w10), .out11(w11), .out12(w12), .out13(w13), .out14(w14), .out15(w15),
    .out16(w16), .out17(w17), .out18(w18), .out19(w19), .out20(w20), .out21(w21), .out22(w22), .out23(w23),
    .out24(w24), .out25(w25), .out26(w26), .out27(w27), .out28(w28), .out29(w29), .out30(w30), .out31(w31),
    .in(RegWEn), .sel(rd));
  Register #(.width(32)) register_1 (.D(Write_Data), .en(w0), .clk(clk), .Q(x0));  // open: clr
  Register #(.width(32)) register_2 (.D(Write_Data), .en(w4), .clk(clk), .Q(x4));  // open: clr
  Register #(.width(32)) register_3 (.D(Write_Data), .en(w8), .clk(clk), .Q(s0));  // open: clr
  Register #(.width(32)) register_4 (.D(Write_Data), .en(w12), .clk(clk), .Q(x12));  // open: clr
  Register #(.width(32)) register_5 (.D(Write_Data), .en(w16), .clk(clk), .Q(x16));  // open: clr
  Register #(.width(32)) register_6 (.D(Write_Data), .en(w20), .clk(clk), .Q(x20));  // open: clr
  Register #(.width(32)) register_7 (.D(Write_Data), .en(w24), .clk(clk), .Q(x24));  // open: clr
  Register #(.width(32)) register_8 (.D(Write_Data), .en(w28), .clk(clk), .Q(x28));  // open: clr
  Register #(.width(32)) register_9 (.D(Write_Data), .en(w1), .clk(clk), .Q(ra));  // open: clr
  Register #(.width(32)) register_10 (.D(Write_Data), .en(w5), .clk(clk), .Q(t0));  // open: clr
  Register #(.width(32)) register_11 (.D(Write_Data), .en(w9), .clk(clk), .Q(s1));  // open: clr
  Register #(.width(32)) register_12 (.D(Write_Data), .en(w13), .clk(clk), .Q(x13));  // open: clr
  Register #(.width(32)) register_13 (.D(Write_Data), .en(w17), .clk(clk), .Q(x17));  // open: clr
  Register #(.width(32)) register_14 (.D(Write_Data), .en(w21), .clk(clk), .Q(x21));  // open: clr
  Register #(.width(32)) register_15 (.D(Write_Data), .en(w25), .clk(clk), .Q(x25));  // open: clr
  Register #(.width(32)) register_16 (.D(Write_Data), .en(w29), .clk(clk), .Q(x29));  // open: clr
  Register #(.width(32)) register_17 (.D(Write_Data), .en(w2), .clk(clk), .Q(sp));  // open: clr
  Register #(.width(32)) register_18 (.D(Write_Data), .en(w6), .clk(clk), .Q(t1));  // open: clr
  Register #(.width(32)) register_19 (.D(Write_Data), .en(w10), .clk(clk), .Q(a0));  // open: clr
  Register #(.width(32)) register_20 (.D(Write_Data), .en(w14), .clk(clk), .Q(x14));  // open: clr
  Register #(.width(32)) register_21 (.D(Write_Data), .en(w18), .clk(clk), .Q(x18));  // open: clr
  Register #(.width(32)) register_22 (.D(Write_Data), .en(w22), .clk(clk), .Q(x22));  // open: clr
  Register #(.width(32)) register_23 (.D(Write_Data), .en(w26), .clk(clk), .Q(x26));  // open: clr
  Register #(.width(32)) register_24 (.D(Write_Data), .en(w30), .clk(clk), .Q(x30));  // open: clr
  Register #(.width(32)) register_25 (.D(Write_Data), .en(w3), .clk(clk), .Q(x3));  // open: clr
  Register #(.width(32)) register_26 (.D(Write_Data), .en(w7), .clk(clk), .Q(t2));  // open: clr
  Register #(.width(32)) register_27 (.D(Write_Data), .en(w11), .clk(clk), .Q(x11));  // open: clr
  Register #(.width(32)) register_28 (.D(Write_Data), .en(w15), .clk(clk), .Q(x15));  // open: clr
  Register #(.width(32)) register_29 (.D(Write_Data), .en(w19), .clk(clk), .Q(x19));  // open: clr
  Register #(.width(32)) register_30 (.D(Write_Data), .en(w23), .clk(clk), .Q(x23));  // open: clr
  Register #(.width(32)) register_31 (.D(Write_Data), .en(w27), .clk(clk), .Q(x27));  // open: clr
  Register #(.width(32)) register_32 (.D(Write_Data), .en(w31), .clk(clk), .Q(x31));  // open: clr

  // Other names for the same wires on the sheet: read_data1[31:0] = Read_Data_1; read_data2[31:0] = Read_Data_2;
  //   read_reg1[4:0] = rs1; read_reg2[4:0] = rs2; write_en = RegWEn; write_reg[4:0] = rd; x1[31:0] = ra;
  //   x2[31:0] = sp; x5[31:0] = t0; x6[31:0] = t1; x7[31:0] = t2; x8[31:0] = s0; x9[31:0] = s1; x10[31:0] = a0

  // Notes on the sheet:
  //   INPUTS to your circuit
  //   DON'T CHANGE THE LOCATIONS OF THE INPUTS AND OUTPUTS!
  //   These are DEBUG/TEST outputs from your circuit.
  //   OUTPUTS from your circuit
endmodule
